// Digital circuit BRAM.dig as structural Verilog
module BRAM (
  input  in_1,
  input  in_2,
  input  in_3,
  input  [3:0] in_4,
  input  [15:0] in_5,
  input  clk,
  input  clk_2,
  input  in_13,
  input  clk_3,
  output [15:0] out_8,
  output out_9,
  output out_10,
  output out_11,
  output out_12
);

  simple_dual_two_clocks #(.applicationType("GHDL")) u_simple_dual_two_clocks (
    .clka(clk), .clkb(clk_2), .ena(in_1), .enb(in_2), .wea(in_3), .addra({out_12, out_11, out_10, out_9}),
    .addrb(in_4), .dia(in_5), .dob(out_8));
  _7493 _7493_1 (
    .pin1(out_9), .pin2(1'b1), .pin3(in_13), .pin5(1'b1), .pin8(out_11), .pin9(out_10), .pin10(1'b0),
    .pin11(out_12), .pin12(out_9), .pin14(clk_3));  // open: pin4, pin6, pin7, pin13

  // Other names for the same wires on the sheet: _0[15:0] = in_5

  // Notes on the sheet:
  //   clk_2: Hz: 5
endmodule

/* Code of simple_dual_two_clocks:
-- Simple Dual-Port Block RAM with Two Clocks
-- Correct Modelization with a Shared Variable
-- File: simple_dual_two_clocks.vhd
library IEEE;
use IEEE.std_logic_1164.all;
use IEEE.std_logic_unsigned.all;

entity simple_dual_two_clocks is
 port(
 clka : in std_logic;
 clkb : in std_logic;
 ena : in std_logic;
 enb : in std_logic;
 wea : in std_logic;
 addra : in std_logic_vector(3 downto 0);
 addrb : in std_logic_vector(3 downto 0);
 dia : in std_logic_vector(15 downto 0);
 dob : out std_logic_vector(15 downto 0)
 );
end simple_dual_two_clocks;

architecture syn of simple_dual_two_clocks is
 type ram_type is array (1023 downto 0) of std_logic_vector(15 downto 0);
 signal RAM : ram_type;
 
begin
 process(clka)
 begin
 if clka'event and clka = '1' then
	if ena = '1' then
		if wea = '1' then
			RAM(conv_integer(addra)) <= dia;
		end if;
	end if;
 end if;
 end process;
 
 
 process(clkb)
 begin
 if clkb'event and clkb = '1' then
	if enb = '1' then
		dob <= RAM(conv_integer(addrb));
		end if;
	end if;
 end process;
 
end syn;
*/
