// Digital circuit BRAM.dig as structural Verilog
module BRAM (
  input  in_1,
  input  in_2,
  input  in_3,
  input  [3:0] in_4,
  input  [15:0] in_5,
  input  clk,
  input  clk_2,
  input  in_13,
  input  clk_3,
  input  in_15,
  input  in_16,
  input  [2:0] in_17,
  input  [15:0] in_18,
  input  [15:0] in_19,
  input  [15:0] in_20,
  output [15:0] out_8,
  output out_9,
  output out_10,
  output out_11,
  output out_12,
  output [2:0] out_21,
  output [15:0] out_22,
  output [15:0] out_23
);

  switch #(.applicationType("GHDL")) u_switch (
    .clk(in_15), .rst_n(in_16), .index_PE(in_17), .cc1_max(in_18), .cc2_MAX(in_19), .cc3_MAX(in_20),
    .index_out(out_21), .delta1(out_22), .delta2(out_23));
  simple_dual_two_clocks #(.applicationType("GHDL")) u_simple_dual_two_clocks (
    .clka(clk), .clkb(clk_2), .ena(in_1), .enb(in_2), .wea(in_3), .addra({out_12, out_11, out_10, out_9}),
    .addrb(in_4), .dia(in_5), .dob(out_8));
  _7493 _7493_1 (
    .pin1(out_9), .pin2(1'b1), .pin3(in_13), .pin5(1'b1), .pin8(out_11), .pin9(out_10), .pin10(1'b0),
    .pin11(out_12), .pin12(out_9), .pin14(clk_3));  // open: pin4, pin6, pin7, pin13

  // Other names for the same wires on the sheet: _0[15:0] = in_5

  // Notes on the sheet:
  //   clk_2: Hz: 5
endmodule

/* Code of switch:
-- switcher description: we get indexer from power max. This will then help us find the neighbouring mics. 
-- If indexer is 2 we know that 1, 2, 3 are affected. Therefore, we take the cc1 and cc2, because cc1 have 2-1 and (-)cc2 have 2-3
--    cc1: mics 1 and 2
--    cc2: mics 2 and 3 
-- (-)cc2: mics 3 and 2
--    cc3: mics 3 and 4
-- we output the two delta values being the max value from each correlation and the common index_out from the cross-corelation.

library IEEE;
use IEEE.STD_LOGIC_1164.ALL;
use ieee.std_logic_unsigned.all;
use IEEE.NUMERIC_STD.ALL;


ENTITY switch IS
  PORT  (
    clk			: IN STD_LOGIC ;
	rst_n 		: IN STD_LOGIC;
	index_PE  	: IN STD_LOGIC_VECTOR (2 downto 0);
	cc1_max 	: IN STD_LOGIC_VECTOR (15 downto 0);
	cc2_MAX 	: IN STD_LOGIC_VECTOR (15 downto 0);
	cc3_MAX 	: IN STD_LOGIC_VECTOR (15 downto 0);
	index_out	: OUT STD_LOGIC_VECTOR (2 downto 0);
	delta1		: OUT STD_LOGIC_VECTOR (15 downto 0);
    delta2 		: out std_logic_vector (15 downto 0)  
    );
END ENTITY switch;

ARCHITECTURE ARCH_switch OF switch IS

  SIGNAL delta1_out_signal: STD_LOGIC_VECTOR (15 DOWNTO 0);
  SIGNAL delta2_out_signal: STD_LOGIC_VECTOR (15 DOWNTO 0);
  begin
  
--  delta1_out_signal <=   (cc1_max + (conv_integer(index_PE) < 3)) 
--						 + (cc2_MAX + (conv_integer(index_PE) >= 3));
--  delta2_out_signal <=   (cc2_MAX + (conv_integer(index_PE) < 3)) 
-- 					     + (cc3_MAX +(conv_integer(index_PE) >= 3));
    delta1_out_signal <= cc1_max when (conv_integer(index_PE) < 3) else
						 cc2_MAX;
    
	delta2_out_signal <= cc2_max when (conv_integer(index_PE) < 3) else
						 cc3_MAX;
 
 delta1 <= delta1_out_signal;
 delta2 <= delta2_out_signal;

END ARCH_switch;
*/

/* Code of simple_dual_two_clocks:
-- Simple Dual-Port Block RAM with Two Clocks
-- Correct Modelization with a Shared Variable
-- File: simple_dual_two_clocks.vhd
library IEEE;
use IEEE.std_logic_1164.all;
use IEEE.std_logic_unsigned.all;

entity simple_dual_two_clocks is
 port(
 clka : in std_logic;
 clkb : in std_logic;
 ena : in std_logic;
 enb : in std_logic;
 wea : in std_logic;
 addra : in std_logic_vector(3 downto 0);
 addrb : in std_logic_vector(3 downto 0);
 dia : in std_logic_vector(15 downto 0);
 dob : out std_logic_vector(15 downto 0)
 );
end simple_dual_two_clocks;

architecture syn of simple_dual_two_clocks is
 type ram_type is array (1023 downto 0) of std_logic_vector(15 downto 0);
 signal RAM : ram_type;
 
begin
 process(clka)
 begin
 if clka'event and clka = '1' then
	if ena = '1' then
		if wea = '1' then
			RAM(conv_integer(addra)) <= dia;
		end if;
	end if;
 end if;
 end process;
 
 
 process(clkb)
 begin
 if clkb'event and clkb = '1' then
	if enb = '1' then
		dob <= RAM(conv_integer(addrb));
		end if;
	end if;
 end process;
 
end syn;
*/
